// Logisim project 16BitCPU.circ as structural Verilog: 12 circuits, main circuit main
module main (
  input  Reset,
  input  Enable
);

  wire ALU_Enable, and_1_out, Clock, Comp, Comp_Jump_NOP, Immediate, JC, JE, JG, JGE, JL, JLE, JN, JNC, JNE,
       JNN, JNO, JNP, JNZ, JO, JP, Jump, JZ, LD, multiplexer_1_out, NOP, or_2_out, or_3_out, RegWr, RES,
       Reset_t, STR;
  wire [1:0] OpSelect;
  wire [3:0] ALU_Opcode, Condition, multiplexer_5_out, z;
  wire [4:0] alu_1_status;
  wire [5:0] comparator_1_gt;
  wire [11:0] Immediate_Addr, multiplexer_2_out, multiplexer_6_out, program_counter_1_pc, register_file_1_ry;
  wire [15:0] alu_1_y, multiplexer_3_out, multiplexer_4_out, ram_1_data, register_file_1_rx;
  wire [15:12] Immediate_Value, register_file_1_ry_2;

  Multiplexer #(.select(4), .disabled(0)) multiplexer_1 (
    .in0(JG), .in1(JGE), .in2(JE), .in3(JNE), .in4(JLE), .in5(JL), .in6(JC), .in7(JZ), .in8(JN), .in9(JO),
    .in10(JP), .in11(JNC), .in12(JNZ), .in13(JNN), .in14(JNO), .in15(JNP), .out(multiplexer_1_out),
    .sel(Condition), .en(Jump));
  Multiplexer #(.width(12), .disabled(0)) multiplexer_2 (
    .in0(register_file_1_ry), .in1(Immediate_Addr), .out(multiplexer_2_out), .sel(Immediate), .en(Jump));
  Program_Counter program_counter_1 (
    .clk(Clock), .clr(Reset_t), .Jump(multiplexer_1_out), .Jump_Addr(multiplexer_2_out),
    .PC(program_counter_1_pc), .Enable(Enable));
  Demultiplexer #(.select(2), .disabled(0)) demultiplexer_1 (
    .out0(ALU_Enable), .out1(LD), .out2(STR), .out3(Comp_Jump_NOP), .in(1'b1), .sel(OpSelect), .en(Enable));
  Clock u_Clock (.out(Clock));
  or or_1 (Reset_t, Reset, RES);
  ROM #(.addrWidth(12), .dataWidth(32)) rom_1 (
    .addr(program_counter_1_pc),
    .data({Immediate, RegWr, Condition, Immediate_Value, Immediate_Addr, z, ALU_Opcode, OpSelect}),
    .sel(Enable));
  Demultiplexer #(.select(2), .disabled(0)) demultiplexer_2 (
    .out0(RES), .out1(Comp), .out2(Jump), .out3(NOP), .in(Comp_Jump_NOP), .sel(ALU_Opcode[1:0]), .en(Enable));
  or or_2 (or_2_out, LD, ALU_Enable);
  Multiplexer #(.width(16), .disabled(0)) multiplexer_3 (
    .in0(alu_1_y), .in1({Immediate_Value, Immediate_Addr}), .out(multiplexer_3_out), .sel(Immediate),
    .en(Enable));
  and and_1 (and_1_out, or_2_out, RegWr);
  Multiplexer #(.width(16), .disabled(0)) multiplexer_4 (
    .in0(multiplexer_3_out), .in1(ram_1_data), .out(multiplexer_4_out), .sel(LD), .en(RegWr));
  Register_File register_file_1 (
    .Rz(multiplexer_4_out), .Rx(register_file_1_rx), .Ry({register_file_1_ry_2, register_file_1_ry}),
    .write(and_1_out), .z(z), .clk(Clock), .reset(Reset_t), .read(Enable), .x(multiplexer_5_out),
    .y(Immediate_Addr[7:4]));
  Multiplexer #(.width(4), .disabled(0)) multiplexer_5 (
    .in0(Immediate_Addr[3:0]), .in1(z), .out(multiplexer_5_out), .sel(STR), .en(Enable));
  Multiplexer #(.width(12)) multiplexer_6 (
    .in0(register_file_1_ry), .in1(Immediate_Addr), .out(multiplexer_6_out), .sel(Immediate), .en(or_3_out));
  or or_3 (or_3_out, LD, STR);
  ALU alu_1 (
    .Y(alu_1_y), .Opcode(ALU_Opcode), .Enable(ALU_Enable), .Status(alu_1_status), .A(register_file_1_rx),
    .B({register_file_1_ry_2, register_file_1_ry}));
  Comparator #(.width(16)) comparator_1 (
    .a(register_file_1_rx), .b({register_file_1_ry_2, register_file_1_ry}), .gt(comparator_1_gt[0]),
    .eq(comparator_1_gt[2]), .lt(comparator_1_gt[5]));
  RAM #(.addrWidth(12), .dataWidth(16)) ram_1 (
    .addr(multiplexer_6_out), .data(ram_1_data), .sel(or_3_out), .clk(Clock), .ld(LD), .clr(Reset_t));
  Register #(.width(5), .trigger("falling")) CPSR (
    .D(alu_1_status), .en(Enable), .Q({JP, JO, JN, JZ, JC}), .clk(Clock), .clr(Reset_t));
  or or_4 (comparator_1_gt[1], comparator_1_gt[0], comparator_1_gt[2]);
  or or_5 (comparator_1_gt[4], comparator_1_gt[2], comparator_1_gt[5]);
  assign ram_1_data = STR ? register_file_1_rx : 16'bz;  // Controlled_Buffer controlled_buffer_1
  not not_1 (comparator_1_gt[3], comparator_1_gt[2]);
  not not_2 (JNC, JC);
  not not_3 (JNZ, JZ);
  not not_4 (JNN, JN);
  not not_5 (JNO, JO);
  not not_6 (JNP, JP);
  Register #(.width(6), .trigger("falling")) register_1 (
    .D(comparator_1_gt), .en(Comp), .Q({JL, JLE, JNE, JE, JGE, JG}), .clk(Clock), .clr(Reset_t));

  // Other names for the same wires on the sheet: OpSelect2[1:0] = ALU_Opcode[1:0];
  //   Immediate_Value[11:0] = Immediate_Addr; x[3:0] = Immediate_Addr[3:0]; y[3:0] = Immediate_Addr[7:4]

  // Notes on the sheet:
  //   ROM
  //   contents of rom_1 (hex, n*v repeats v):
  //   c0000014 c0000854 c0000494 c3fffcd4 c03ffd14 8001b902 4000000c 8001b802 0 0 8001b8c2 3
  //   RAM
endmodule

module Arithmetic_Shift_Right (
  input  [15:0] in_1,
  input  [3:0] in_2,
  output [15:0] out_3
);

  wire [15:15] shifter_1_out;

  Shifter #(.width(16), .shift("lr")) shifter_1 (.in(in_1), .\dist (in_2), .out({shifter_1_out[15], out_3[14:0]}));

  assign out_3[15] = in_1[15];
endmodule

module Shift_Left (
  input  [15:0] in_1,
  input  [3:0] in_2,
  output [15:0] out_3,
  output Cout
);

  wire or_1_out, or_2_out, or_3_out, or_4_out, or_5_out, or_6_out, or_7_out, or_8_out, or_9_out, or_10_out,
       or_11_out, or_12_out, or_13_out, or_14_out;

  Shifter #(.width(16)) shifter_1 (.in(in_1), .\dist (in_2), .out(out_3));
  or or_1 (or_1_out, in_1[15], in_1[14]);
  or or_2 (or_2_out, or_1_out, in_1[13]);
  or or_3 (or_3_out, or_2_out, in_1[12]);
  or or_4 (or_4_out, or_3_out, in_1[11]);
  or or_5 (or_5_out, or_4_out, in_1[10]);
  or or_6 (or_6_out, or_5_out, in_1[9]);
  or or_7 (or_7_out, or_6_out, in_1[8]);
  or or_8 (or_8_out, or_7_out, in_1[7]);
  or or_9 (or_9_out, or_8_out, in_1[6]);
  or or_10 (or_10_out, or_9_out, in_1[5]);
  or or_11 (or_11_out, or_10_out, in_1[4]);
  or or_12 (or_12_out, or_11_out, in_1[3]);
  or or_13 (or_13_out, or_12_out, in_1[2]);
  or or_14 (or_14_out, or_13_out, in_1[1]);
  Multiplexer #(.select(4)) multiplexer_1 (
    .in0(1'b1), .in1(in_1[15]), .in2(or_1_out), .in3(or_2_out), .in4(or_3_out), .in5(or_4_out),
    .in6(or_5_out), .in7(or_6_out), .in8(or_7_out), .in9(or_8_out), .in10(or_9_out), .in11(or_10_out),
    .in12(or_11_out), .in13(or_12_out), .in14(or_13_out), .in15(or_14_out), .out(Cout), .sel(in_2), .en(1'b1));
endmodule

module Logical_Shift_Right (
  input  [15:0] in_1,
  input  [3:0] in_2,
  output [15:0] out_3
);

  Shifter #(.width(16), .shift("lr")) shifter_1 (.in(in_1), .\dist (in_2), .out(out_3));
endmodule

module Odd_Parity (
  input  [15:0] in_1,
  output out_2
);

  xor xor_1 (out_2, in_1[0], in_1[1], in_1[2], in_1[3], in_1[4], in_1[5], in_1[6], in_1[7], in_1[8], in_1[9], in_1[10], in_1[11], in_1[12], in_1[13], in_1[14], in_1[15]);
endmodule

module ALU (
  input  [15:0] A,
  input  [15:0] B,
  input  [3:0] Opcode,
  input  Enable,
  output [4:0] Status,
  output [15:0] Y
);

  wire adder_1_cout, adder_2_cout, shift_left_1_cout, shift_left_2_cout, subtractor_1_bout,
       subtractor_2_bout, xor_2_out;
  wire [15:0] adder_1_out, adder_2_out, and_1_out, arithmetic_shift_right_1_out_3,
       logical_shift_right_1_out_3, negator_1_out, not_1_out, or_1_out, shift_left_1_out_3,
       shift_left_2_out_3, shifter_1_out, shifter_2_out, subtractor_1_out, subtractor_2_out, xor_1_out;

  // Probe on A
  // Probe on B
  Adder #(.width(16)) adder_1 (.a(A), .b(B), .out(adder_1_out), .cin(1'b0), .cout(adder_1_cout));
  Subtractor #(.width(16)) subtractor_1 (.a(A), .b(B), .out(subtractor_1_out), .bin(1'b0), .bout(subtractor_1_bout));
  Negator #(.width(16)) negator_1 (.in(A), .out(negator_1_out));
  Adder #(.width(16)) adder_2 (.a(A), .b({16{1'b0}}), .out(adder_2_out), .cin(1'b1), .cout(adder_2_cout));
  Subtractor #(.width(16)) subtractor_2 (
    .a(A), .b({16{1'b0}}), .out(subtractor_2_out), .bin(1'b1), .bout(subtractor_2_bout));
  assign and_1_out = A & B;  // AND_Gate and_1, 16 bits wide
  assign or_1_out = A | B;  // OR_Gate or_1, 16 bits wide
  assign xor_1_out = A ^ B;  // XOR_Gate xor_1, 16 bits wide
  assign not_1_out = ~A;  // NOT_Gate not_1, 16 bits wide
  Arithmetic_Shift_Right arithmetic_shift_right_1 (.in_1(A), .in_2(B[3:0]), .out_3(arithmetic_shift_right_1_out_3));
  Shift_Left shift_left_1 (.in_1(A), .out_3(shift_left_1_out_3), .in_2(B[3:0]), .Cout(shift_left_1_cout));
  Logical_Shift_Right logical_shift_right_1 (.in_1(A), .in_2(B[3:0]), .out_3(logical_shift_right_1_out_3));
  Shift_Left shift_left_2 (.in_1(A), .out_3(shift_left_2_out_3), .in_2(B[3:0]), .Cout(shift_left_2_cout));
  Shifter #(.width(16), .shift("rr")) shifter_1 (.in(A), .\dist (B[3:0]), .out(shifter_1_out));
  Shifter #(.width(16), .shift("rl")) shifter_2 (.in(A), .\dist (B[3:0]), .out(shifter_2_out));
  // Probe on Opcode
  Multiplexer #(.select(4), .disabled(0)) multiplexer_1 (
    .in0(adder_1_cout), .in1(subtractor_1_bout), .in2(1'b0), .in3(adder_2_cout), .in4(subtractor_2_bout),
    .in5(1'b0), .in6(1'b0), .in7(1'b0), .in8(1'b0), .in9(1'b0), .in10(1'b0), .in11(shift_left_1_cout),
    .in12(1'b0), .in13(shift_left_2_cout), .in14(1'b0), .in15(1'b0), .out(Status[0]), .sel(Opcode),
    .en(Enable));
  Multiplexer #(.select(4), .width(16), .disabled(0)) multiplexer_2 (
    .in0(adder_1_out), .in1(subtractor_1_out), .in2(negator_1_out), .in3(adder_2_out),
    .in4(subtractor_2_out), .in5(A), .in6(and_1_out), .in7(or_1_out), .in8(xor_1_out), .in9(not_1_out),
    .in10(arithmetic_shift_right_1_out_3), .in11(shift_left_1_out_3), .in12(logical_shift_right_1_out_3),
    .in13(shift_left_2_out_3), .in14(shifter_1_out), .in15(shifter_2_out), .out({Status[2], Y[14:0]}),
    .sel(Opcode), .en(Enable));
  xor xor_2 (xor_2_out, Status[0], Status[2]);
  Odd_Parity odd_parity_1 (.in_1({Status[2], Y[14:0]}), .out_2(Status[4]));
  nor nor_1 (Status[1], Y[0], Y[1], Y[2], Y[3], Y[4], Y[5], Y[6], Y[7], Y[8], Y[9], Y[10], Y[11], Y[12], Y[13], Y[14], Status[2]);
  Multiplexer #(.select(4), .disabled(0)) multiplexer_3 (
    .in0(xor_2_out), .in1(xor_2_out), .in2(1'b0), .in3(xor_2_out), .in4(xor_2_out), .in5(1'b0), .in6(1'b0),
    .in7(1'b0), .in8(1'b0), .in9(1'b0), .in10(1'b0), .in11(1'b0), .in12(1'b0), .in13(1'b0), .in14(1'b0),
    .in15(1'b0), .out(Status[3]), .sel(Opcode), .en(Enable));
  // Probe on {Status[2], Y[14:0]}
  // Probe on Status[0]
  // Probe on Status[1]
  // Probe on Status[2]
  // Probe on Status[3]
  // Probe on Status[4]

  assign Y[15] = Status[2];

  // Notes on the sheet:
  //   Circular Shift Right
  //   Circular Shift Left
endmodule

module Register_File (
  input  [15:0] Rz,
  input  clk,
  input  reset,
  input  read,
  input  [3:0] x,
  input  [3:0] y,
  input  write,
  input  [3:0] z,
  output [15:0] Rx,
  output [15:0] Ry
);

  wire demultiplexer_1_out0, demultiplexer_1_out1, demultiplexer_1_out2, demultiplexer_1_out3,
       demultiplexer_1_out4, demultiplexer_1_out5, demultiplexer_1_out6, demultiplexer_1_out7,
       demultiplexer_1_out8, demultiplexer_1_out9, demultiplexer_1_out10, demultiplexer_1_out11,
       demultiplexer_1_out12, demultiplexer_1_out13, demultiplexer_1_out14, demultiplexer_1_out15;
  wire [15:0] ACC0_q, ACC1_q, ACC2_q, ACC3_q, R0_q, R1_q, R2_q, R3_q, R4_q, R5_q, R6_q, R7_q, R8_q, R9_q,
       R10_q, R11_q;

  Demultiplexer #(.select(4), .disabled(0), .enable("false")) demultiplexer_1 (
    .out0(demultiplexer_1_out0), .out1(demultiplexer_1_out1), .out2(demultiplexer_1_out2),
    .out3(demultiplexer_1_out3), .out4(demultiplexer_1_out4), .out5(demultiplexer_1_out5),
    .out6(demultiplexer_1_out6), .out7(demultiplexer_1_out7), .out8(demultiplexer_1_out8),
    .out9(demultiplexer_1_out9), .out10(demultiplexer_1_out10), .out11(demultiplexer_1_out11),
    .out12(demultiplexer_1_out12), .out13(demultiplexer_1_out13), .out14(demultiplexer_1_out14),
    .out15(demultiplexer_1_out15), .in(write), .sel(z));
  Register #(.width(16)) R0 (.D(Rz), .en(demultiplexer_1_out0), .Q(R0_q), .clk(clk), .clr(reset));
  Register #(.width(16)) R1 (.D(Rz), .en(demultiplexer_1_out1), .Q(R1_q), .clk(clk), .clr(reset));
  Register #(.width(16)) R2 (.D(Rz), .en(demultiplexer_1_out2), .Q(R2_q), .clk(clk), .clr(reset));
  Register #(.width(16)) R3 (.D(Rz), .en(demultiplexer_1_out3), .Q(R3_q), .clk(clk), .clr(reset));
  Register #(.width(16)) R4 (.D(Rz), .en(demultiplexer_1_out4), .Q(R4_q), .clk(clk), .clr(reset));
  Register #(.width(16)) R5 (.D(Rz), .en(demultiplexer_1_out5), .Q(R5_q), .clk(clk), .clr(reset));
  Register #(.width(16)) R6 (.D(Rz), .en(demultiplexer_1_out6), .Q(R6_q), .clk(clk), .clr(reset));
  Register #(.width(16)) R7 (.D(Rz), .en(demultiplexer_1_out7), .Q(R7_q), .clk(clk), .clr(reset));
  Register #(.width(16)) R8 (.D(Rz), .en(demultiplexer_1_out8), .Q(R8_q), .clk(clk), .clr(reset));
  Register #(.width(16)) R9 (.D(Rz), .en(demultiplexer_1_out9), .Q(R9_q), .clk(clk), .clr(reset));
  Register #(.width(16)) R10 (.D(Rz), .en(demultiplexer_1_out10), .Q(R10_q), .clk(clk), .clr(reset));
  Register #(.width(16)) R11 (.D(Rz), .en(demultiplexer_1_out11), .Q(R11_q), .clk(clk), .clr(reset));
  Register #(.width(16)) ACC0 (.D(Rz), .en(demultiplexer_1_out12), .Q(ACC0_q), .clk(clk), .clr(reset));
  Register #(.width(16)) ACC1 (.D(Rz), .en(demultiplexer_1_out13), .Q(ACC1_q), .clk(clk), .clr(reset));
  Register #(.width(16)) ACC2 (.D(Rz), .en(demultiplexer_1_out14), .Q(ACC2_q), .clk(clk), .clr(reset));
  Register #(.width(16)) ACC3 (.D(Rz), .en(demultiplexer_1_out15), .Q(ACC3_q), .clk(clk), .clr(reset));
  Multiplexer #(.select(4), .width(16), .disabled(0)) multiplexer_1 (
    .in0(R0_q), .in1(R1_q), .in2(R2_q), .in3(R3_q), .in4(R4_q), .in5(R5_q), .in6(R6_q), .in7(R7_q),
    .in8(R8_q), .in9(R9_q), .in10(R10_q), .in11(R11_q), .in12(ACC0_q), .in13(ACC1_q), .in14(ACC2_q),
    .in15(ACC3_q), .out(Rx), .sel(x), .en(read));
  Multiplexer #(.select(4), .width(16), .disabled(0)) multiplexer_2 (
    .in0(R0_q), .in1(R1_q), .in2(R2_q), .in3(R3_q), .in4(R4_q), .in5(R5_q), .in6(R6_q), .in7(R7_q),
    .in8(R8_q), .in9(R9_q), .in10(R10_q), .in11(R11_q), .in12(ACC0_q), .in13(ACC1_q), .in14(ACC2_q),
    .in15(ACC3_q), .out(Ry), .sel(y), .en(read));
endmodule

module Program_Counter (
  input  [11:0] Jump_Addr,
  input  Jump,
  input  Enable,
  input  clk,
  input  clr,
  output [11:0] PC
);

  wire and_1_out, and_2_out, comparator_1_eq, not_1_out, not_2_out, not_3_out, or_1_out, register_2_q;
  wire [11:0] register_1_q;

  not not_1 (not_1_out, or_1_out);
  Register #(.width(12)) register_1 (.D(Jump_Addr), .en(not_1_out), .Q(register_1_q), .clk(clk), .clr(or_1_out));
  Register #(.width(1)) register_2 (.D(Jump), .en(not_2_out), .Q(register_2_q), .clk(clk), .clr(or_1_out));
  not not_2 (not_2_out, register_2_q);
  not not_3 (not_3_out, register_2_q);
  or or_1 (or_1_out, comparator_1_eq, clr);
  and and_1 (and_1_out, register_2_q, Enable);
  Counter #(.width(12), .max('hfff), .trigger("falling")) Counter (
    .load(and_1_out), .D(register_1_q), .count(and_2_out), .Q(PC), .clk(clk), .clr(clr));  // open: carry
  and and_2 (and_2_out, not_3_out, Enable);
  Comparator #(.width(12)) comparator_1 (.a(register_1_q), .b(PC), .eq(comparator_1_eq));  // open: gt, lt
endmodule

module ALUTesting (
  input  in_1,
  input  in_2,
  input  in_3,
  input  in_4,
  input  in_5
);

  wire d_ff_1_q, d_ff_2_q, not_1_out, not_2_out;
  wire [4:0] alu_1_status, alu_2_status, alu_3_status, alu_4_status, alu_5_status, alu_6_status, alu_7_status;
  wire [15:0] alu_1_y, alu_2_y, alu_3_y, alu_4_y, alu_5_y, alu_6_y, alu_7_y;

  not not_1 (not_1_out, in_1);
  not not_2 (not_2_out, not_1_out);
  D_Flip_Flop_part #(.trigger("high")) d_ff_1 (
    .clk(not_1_out), .D(in_2), .Q(d_ff_1_q), .preset(in_3), .en(in_4), .reset(in_5));  // open: Qn
  D_Flip_Flop_part #(.trigger("high")) d_ff_2 (
    .clk(not_2_out), .D(d_ff_1_q), .Q(d_ff_2_q), .preset(in_3), .en(in_4), .reset(in_5));  // open: Qn
  ALU alu_1 (.Y(alu_1_y), .Opcode(4'b0111), .Enable(1'b1), .Status(alu_1_status), .A(16'he238), .B(16'h5c11));
  ALU alu_2 (.Y(alu_2_y), .Opcode(4'b1111), .Enable(1'b1), .Status(alu_2_status), .A(16'hd733), .B(16'h9df1));
  ALU alu_3 (.Y(alu_3_y), .Opcode(4'b0111), .Enable(1'b1), .Status(alu_3_status), .A(16'hddb9), .B(16'hc22d));
  ALU alu_4 (.Y(alu_4_y), .Opcode(4'b1010), .Enable(1'b1), .Status(alu_4_status), .A(16'he7d), .B(16'hff35));
  ALU alu_5 (.Y(alu_5_y), .Opcode(4'b0111), .Enable(1'b1), .Status(alu_5_status), .A(16'h880f), .B(16'h2a2c));
  ALU alu_6 (.Y(alu_6_y), .Opcode(4'b1011), .Enable(1'b1), .Status(alu_6_status), .A(16'h9a5c), .B(16'h327b));
  ALU alu_7 (.Y(alu_7_y), .Opcode(4'b0001), .Enable(1'b1), .Status(alu_7_status), .A(16'hbf56), .B(16'h9dc9));
  // Probe on alu_1_y
  // Probe on alu_2_y
  // Probe on alu_3_y
  // Probe on alu_4_y
  // Probe on alu_5_y
  // Probe on alu_6_y
  // Probe on alu_7_y
  // Probe on alu_1_status
  // Probe on alu_2_status
  // Probe on alu_3_status
  // Probe on alu_4_status
  // Probe on alu_5_status
  // Probe on alu_6_status
  // Probe on alu_7_status
endmodule

module D_Flip_Flop (
  input  SET,
  input  D,
  input  clk,
  input  CLR,
  output Q,
  output nQ
);

  wire nand_1_out, nand_2_out, not_1_out;

  not not_1 (not_1_out, D);
  nand nand_1 (nand_1_out, D, clk);
  nand nand_2 (nand_2_out, clk, not_1_out);
  nand nand_3 (Q, ~SET, nand_1_out, nQ);  // NAND_Gate
  nand nand_4 (nQ, Q, nand_2_out, ~CLR);  // NAND_Gate
endmodule

module _1_Bit_Register (
  input  D,
  input  clk,
  input  CLR,
  input  SET,
  input  EN,
  output Q
);

  wire and_1_out, d_flip_flop_1_q, not_1_out, not_2_out, or_1_out;

  and and_1 (and_1_out, Q, ~EN);  // AND_Gate
  not not_1 (not_1_out, clk);
  or or_1 (or_1_out, and_1_out, D);
  not not_2 (not_2_out, not_1_out);
  D_Flip_Flop d_flip_flop_1 (.D(or_1_out), .clk(not_1_out), .Q(d_flip_flop_1_q), .SET(SET), .CLR(CLR));  // open: nQ
  D_Flip_Flop d_flip_flop_2 (.D(d_flip_flop_1_q), .clk(not_2_out), .Q(Q), .SET(SET), .CLR(CLR));  // open: nQ
endmodule

module _16_bit_Register (
  input  [15:0] D,
  input  clk,
  input  en,
  input  clr,
  input  set,
  output [15:0] Q
);

  _1_Bit_Register u_1_bit_register_1 (.D(D[0]), .clk(clk), .Q(Q[0]), .SET(set), .CLR(clr), .EN(en));
  _1_Bit_Register u_1_bit_register_2 (.D(D[1]), .clk(clk), .Q(Q[1]), .SET(set), .CLR(clr), .EN(en));
  _1_Bit_Register u_1_bit_register_3 (.D(D[2]), .clk(clk), .Q(Q[2]), .SET(set), .CLR(clr), .EN(en));
  _1_Bit_Register u_1_bit_register_4 (.D(D[3]), .clk(clk), .Q(Q[3]), .SET(set), .CLR(clr), .EN(en));
  _1_Bit_Register u_1_bit_register_5 (.D(D[4]), .clk(clk), .Q(Q[4]), .SET(set), .CLR(clr), .EN(en));
  _1_Bit_Register u_1_bit_register_6 (.D(D[5]), .clk(clk), .Q(Q[5]), .SET(set), .CLR(clr), .EN(en));
  _1_Bit_Register u_1_bit_register_7 (.D(D[6]), .clk(clk), .Q(Q[6]), .SET(set), .CLR(clr), .EN(en));
  _1_Bit_Register u_1_bit_register_8 (.D(D[7]), .clk(clk), .Q(Q[7]), .SET(set), .CLR(clr), .EN(en));
  _1_Bit_Register u_1_bit_register_9 (.D(D[8]), .clk(clk), .Q(Q[8]), .SET(set), .CLR(clr), .EN(en));
  _1_Bit_Register u_1_bit_register_10 (.D(D[9]), .clk(clk), .Q(Q[9]), .SET(set), .CLR(clr), .EN(en));
  _1_Bit_Register u_1_bit_register_11 (.D(D[10]), .clk(clk), .Q(Q[10]), .SET(set), .CLR(clr), .EN(en));
  _1_Bit_Register u_1_bit_register_12 (.D(D[11]), .clk(clk), .Q(Q[11]), .SET(set), .CLR(clr), .EN(en));
  _1_Bit_Register u_1_bit_register_13 (.D(D[12]), .clk(clk), .Q(Q[12]), .SET(set), .CLR(clr), .EN(en));
  _1_Bit_Register u_1_bit_register_14 (.D(D[13]), .clk(clk), .Q(Q[13]), .SET(set), .CLR(clr), .EN(en));
  _1_Bit_Register u_1_bit_register_15 (.D(D[14]), .clk(clk), .Q(Q[14]), .SET(set), .CLR(clr), .EN(en));
  _1_Bit_Register u_1_bit_register_16 (.D(D[15]), .clk(clk), .Q(Q[15]), .SET(set), .CLR(clr), .EN(en));
endmodule
